# Fritzing sketch LightSenser (saved by Fritzing 0.9.5d)
breadboards: 1

parts:
  Part1 = Arduino Uno (Rev3)
  R1 = Photocell (LDR) [package=THT]
  R2 = Resistor [tolerance=±5% resistance=10k package=THT]

nets:
  N1: Part1.A0, Part1.5V, R1.pin_0
  N2: Part1.GND, R2.Pin_1
  N3: R1.pin_1, R2.Pin_0
